# Fritzing sketch Wiring Diagram (saved by Fritzing 0.9.0b)
circuit board: 19.7312cm x 18.7984cm
breadboards: 1

parts:
  part = Arduino Uno (Rev3)
  Red_Button = Pushbutton [package=THT]
  Green_Button = Pushbutton [package=THT]
  R1 = Resistor [tolerance=±5% resistance=10k package=THT]
  R2 = Resistor [tolerance=±5% resistance=10k package=THT]
  12_Position_Rotary_Encoder_(RobotMesh) = ENCODER-QUADRATURE [package=encoder-16mm-quad]

nets:
  N1: part.A0, 12_Position_Rotary_Encoder_(RobotMesh).C
  N2: part.GND, R1.Pin_1, R2.Pin_1, 12_Position_Rotary_Encoder_(RobotMesh).A
  N3: part.D2, Green_Button.leg0, R1.Pin_0
  N4: part.D3_PWM, Red_Button.leg0, R2.Pin_0
  N5: part.5V, Red_Button.leg1, Green_Button.leg1, 12_Position_Rotary_Encoder_(RobotMesh).B
